# Fritzing sketch CNC Plotter (1) (saved by Fritzing 0.9.4)

parts:
  M1 = Dagu DGServo 9g (Top view) [part_number=RS001B]
  X1 = X113647 Stepper Driver Board [package=board]
  MOTOR1 = 28BYJ-48 Stepper Motor
  X2 = X113647 Stepper Driver Board [package=board]
  MOTOR2 = 28BYJ-48 Stepper Motor
  Parça1 = Arduino Uno (Rev3)
  U1 = Mini-USB _B_ connector with 5th pin broken out. [package=usb-minib]

nets:
  N1: M1.pulse, Parça1.D11_PWM/MOSI
  N2: X1.IN1, Parça1.D5_PWM
  N3: X1.IN2, Parça1.D4
  N4: X1.IN3, Parça1.D3_PWM
  N5: X1.IN4, Parça1.D2
  GND: X1.GND, X2.GND, U1.VBUS
  N6: X1.BLUE, MOTOR1.BLUE
  N7: X1.PINK, MOTOR1.PINK
  N8: X1.YELLOW, MOTOR1.RED
  N9: X1.ORANGE, MOTOR1.ORANGE
  N10: X1.RED, MOTOR1.YELLOW
  N11: X2.IN1, Parça1.A3
  N12: X2.IN2, Parça1.A2
  N13: X2.IN3, Parça1.A1
  N14: X2.IN4, Parça1.A0
  N15: X2.+V, U1.D-
  N16: X2.BLUE, MOTOR2.BLUE
  N17: X2.PINK, MOTOR2.PINK
  N18: X2.YELLOW, MOTOR2.RED
  N19: X2.ORANGE, MOTOR2.ORANGE
  N20: X2.RED, MOTOR2.YELLOW

custom parts:
  X113647 Stepper Driver Board: A common stepper motor driver board based on ULN2003APG darlington array
  28BYJ-48 Stepper Motor: 28BYJ-48 gear-reduction stepper motor (small)
